# Fritzing sketch schema_electronique (saved by Fritzing 0.9.3b)
breadboards: 2

parts:
  J2 = Basic Servo
  R4 = Resistor [tolerance=±5% resistance=220 package=THT]  # not connected
  LED2 = LED - 5mm [color="Blue (430nm)" package="5 mm [THT]"]
  U1 = ESP8266 NodeMCU LoLin module
  R5 = Resistor [tolerance=±5% resistance=3.3k package="0805 [SMD]"]
  R6 = Resistor [tolerance=±5% resistance=100 package="0603 [SMD]"]

nets:
  GND: J2.gnd, LED2.cathode, U1.GND
  N1: J2.vcc, U1.VU
  N2: J2.pulse, U1.D4
  N3: LED2.anode, R6.Pin_1
  N4: U1.D0, R5.Pin_0
  N5: U1.D7, R6.Pin_0
  N6: U1.RST, R5.Pin_1

custom parts:
  ESP8266 NodeMCU LoLin module: ESP8266 based NodeMCU
